// Digital circuit 6bitAND.dig as structural Verilog
module _6bitAND (
  input  [5:0] A_5_0,
  input  [5:0] B_5_0,
  output [5:0] R_5_0
);

  and and_1 (R_5_0[5], A_5_0[5], B_5_0[5]);
  and and_2 (R_5_0[4], A_5_0[4], B_5_0[4]);
  and and_3 (R_5_0[3], A_5_0[3], B_5_0[3]);
  and and_4 (R_5_0[2], A_5_0[2], B_5_0[2]);
  and and_5 (R_5_0[1], A_5_0[1], B_5_0[1]);
  and and_6 (R_5_0[0], A_5_0[0], B_5_0[0]);

  // Other names for the same wires on the sheet: A0 = A_5_0[0]; A1 = A_5_0[1]; A2 = A_5_0[2]; A3 = A_5_0[3];
  //   A4 = A_5_0[4]; A5 = A_5_0[5]; B0 = B_5_0[0]; B1 = B_5_0[1]; B2 = B_5_0[2]; B3 = B_5_0[3]; B4 = B_5_0[4];
  //   B5 = B_5_0[5]; R0 = R_5_0[0]; R1 = R_5_0[1]; R2 = R_5_0[2]; R3 = R_5_0[3]; R4 = R_5_0[4]; R5 = R_5_0[5]
endmodule
