// Digital circuit 6bitAdder.dig as structural Verilog
module _6bitAdder (
  input  [5:0] A_5_0,
  input  [5:0] B_5_0,
  output Cout,
  output [5:0] R_5_0
);

  wire adder_2_cout, adder_3_cout, adder_4_cout, adder_5_cout, adder_6_cout;

  Adder adder_1 (.A(A_5_0[5]), .B(B_5_0[5]), .Cin(adder_2_cout), .R(R_5_0[5]), .Cout(Cout));
  Adder adder_2 (.A(A_5_0[4]), .B(B_5_0[4]), .Cin(adder_3_cout), .R(R_5_0[4]), .Cout(adder_2_cout));
  Adder adder_3 (.A(A_5_0[3]), .B(B_5_0[3]), .Cin(adder_4_cout), .R(R_5_0[3]), .Cout(adder_3_cout));
  Adder adder_4 (.A(A_5_0[2]), .B(B_5_0[2]), .Cin(adder_5_cout), .R(R_5_0[2]), .Cout(adder_4_cout));
  Adder adder_5 (.A(A_5_0[1]), .B(B_5_0[1]), .Cin(adder_6_cout), .R(R_5_0[1]), .Cout(adder_5_cout));
  Adder adder_6 (.A(A_5_0[0]), .B(B_5_0[0]), .Cin(1'b0), .R(R_5_0[0]), .Cout(adder_6_cout));
  // Pins of 1 and 6 bits meet at A_5_0
  // Pins of 1 and 6 bits meet at B_5_0
  // Pins of 1 and 6 bits meet at R_5_0
endmodule
