// Digital circuit 6bitReg.dig as structural Verilog
module _6bitReg (
  input  [5:0] Din_5_0,
  input  Sel,
  input  CLK,
  output [5:0] Dout_5_0
);

  _1bitReg _1bitreg_1 (.Din(Din_5_0[5]), .Sel(Sel), .CLK(CLK), .Dout(Dout_5_0[5]));
  _1bitReg _1bitreg_2 (.Din(Din_5_0[4]), .Sel(Sel), .CLK(CLK), .Dout(Dout_5_0[4]));
  _1bitReg _1bitreg_3 (.Din(Din_5_0[3]), .Sel(Sel), .CLK(CLK), .Dout(Dout_5_0[3]));
  _1bitReg _1bitreg_4 (.Din(Din_5_0[2]), .Sel(Sel), .CLK(CLK), .Dout(Dout_5_0[2]));
  _1bitReg _1bitreg_5 (.Din(Din_5_0[1]), .Sel(Sel), .CLK(CLK), .Dout(Dout_5_0[1]));
  _1bitReg _1bitreg_6 (.Din(Din_5_0[0]), .Sel(Sel), .CLK(CLK), .Dout(Dout_5_0[0]));

  // Other names for the same wires on the sheet: B0 = Dout_5_0[0]; B1 = Dout_5_0[1]; B2 = Dout_5_0[2];
  //   B3 = Dout_5_0[3]; B4 = Dout_5_0[4]; B5 = Dout_5_0[5]; A0 = Din_5_0[0]; A1 = Din_5_0[1]; A2 = Din_5_0[2];
  //   A3 = Din_5_0[3]; A4 = Din_5_0[4]; A5 = Din_5_0[5]
endmodule
