// Digital circuit ALUCircuit.dig as structural Verilog
module ALUCircuit (
  input  [5:0] A_5_0,
  input  [5:0] B_5_0,
  input  [1:0] Op_1_0,
  output [5:0] R_5_0
);

  wire [5:0] _6bitadder_1_p3, _6bitand_1_r_5_0, _6bitrol_1_r_5_0;

  // _6bitAdder _6bitadder_1: pin names not known; wires that end beside it: A_5_0, B_5_0, _6bitadder_1_p3
  _6bitAND _6bitand_1 (.A_5_0(A_5_0), .B_5_0(B_5_0), .R_5_0(_6bitand_1_r_5_0));
  _6bitROL _6bitrol_1 (.A_5_0(A_5_0), .B_5_0(B_5_0), .R_5_0(_6bitrol_1_r_5_0));
  Multiplexer #(.Selector_Bits(2), .Bits(6)) multiplexer_1 (
    .sel(Op_1_0), .in_0(_6bitadder_1_p3), .in_1(_6bitand_1_r_5_0), .in_2(_6bitrol_1_r_5_0), .in_3({6{1'b0}}),
    .out(R_5_0));

  // Other names for the same wires on the sheet: A[5:0] = A_5_0; B[5:0] = B_5_0
endmodule
