// Digital circuit Adder.dig as structural Verilog
module Adder (
  input  A,
  input  B,
  input  Cin,
  output R,
  output Cout
);

  wire and_1_out, and_2_out, xor_1_out;

  and and_1 (and_1_out, A, B);
  xor xor_1 (xor_1_out, A, B);
  and and_2 (and_2_out, xor_1_out, Cin);
  xor xor_2 (R, xor_1_out, Cin);
  or or_1 (Cout, and_2_out, and_1_out);

  // Other names for the same wires on the sheet: S = R
endmodule
