// Digital circuit CPU.dig as structural Verilog
module CPU (
  input  [3:0] WR_3_0,
  input  WE,
  input  [16:0] WRD_16_0,
  input  CLK,
  input  PC_EN,
  input  [3:0] RA2_3_0,
  input  ZF,
  output [16:0] RD2_16_0,
  output [1:0] R1_1_0,
  output [1:0] R2_1_0,
  output [1:0] WR_1_0,
  output [5:0] R_5_0,
  output [5:0] A_5_0,
  output [5:0] B_5_0,
  output [5:0] IMM_VAL_5_0,
  output [3:0] JMP_Address
);

  wire CPU_CLK, IMM_SEL, JMP_SEL, REG_EN;
  wire [1:0] Op;
  wire [3:0] _4bitpc_adder_1_o_3_0, _4bitprogcounter_1_o_3_0, multiplexer_1_out;
  wire [4:0] Don_t_care;
  wire [5:0] _6bitregset_1_b_5_0;
  wire [16:13] _9x17ram_1_rd1_16_0;

  Multiplexer #(.Bits(4)) multiplexer_1 (
    .sel(JMP_SEL), .in_0(_4bitpc_adder_1_o_3_0), .in_1({JMP_Address[3:2], IMM_VAL_5_0[5:4]}),
    .out(multiplexer_1_out));
  _4bitPC_Adder _4bitpc_adder_1 (.I_3_0(_4bitprogcounter_1_o_3_0), .O_3_0(_4bitpc_adder_1_o_3_0));
  _4bitProgCounter _4bitprogcounter_1 (.I_3_0(multiplexer_1_out), .CLK(CPU_CLK), .O_3_0(_4bitprogcounter_1_o_3_0));
  and and_1 (CPU_CLK, PC_EN, CLK);
  _9x17RAM _9x17ram_1 (
    .RA1_3_0(_4bitprogcounter_1_o_3_0), .RA2_3_0(RA2_3_0), .WR_3_0(WR_3_0), .WRD_16_0(WRD_16_0), .WE(WE),
    .CLK(CLK), .RD1_16_0({_9x17ram_1_rd1_16_0, JMP_Address[3:2], IMM_VAL_5_0, Don_t_care}),
    .RD2_16_0(RD2_16_0));
  _6bitCU _6bitcu_1 (
    .Opcode_3_0(_9x17ram_1_rd1_16_0), .ZF(ZF), .Op_1_0(Op), .REG_EN(REG_EN), .Imm_Sel(IMM_SEL),
    .Jmp_Sel(JMP_SEL));
  _6bitRegSet _6bitregset_1 (
    .WR_1_0(JMP_Address[3:2]), .CLK(CPU_CLK), .WE(REG_EN), .WRD_5_0(R_5_0), .A_5_0(A_5_0),
    .B_5_0(_6bitregset_1_b_5_0), .RA_1_0(JMP_Address[3:2]), .RB_1_0(IMM_VAL_5_0[5:4]));
  ALUCircuit alucircuit_1 (.A_5_0(A_5_0), .B_5_0(B_5_0), .R_5_0(R_5_0), .Op_1_0(Op));
  Multiplexer #(.Bits(6)) multiplexer_2 (.sel(IMM_SEL), .in_0(_6bitregset_1_b_5_0), .in_1(IMM_VAL_5_0), .out(B_5_0));

  assign JMP_Address[1:0] = IMM_VAL_5_0[5:4];
  assign R1_1_0 = JMP_Address[3:2];
  assign R2_1_0 = IMM_VAL_5_0[5:4];
  assign WR_1_0 = JMP_Address[3:2];

  // Other names for the same wires on the sheet: XX[4:0] = Don_t_care; Don_t_care[8:5] = IMM_VAL_5_0[3:0];
  //   Imm_val[5:0] = IMM_VAL_5_0; R2[1:0] = IMM_VAL_5_0[5:4]; R1[1:0] = JMP_Address[3:2]; A[5:0] = A_5_0;
  //   B[5:0] = B_5_0; R[5:0] = R_5_0; RD2[16:0] = RD2_16_0

  // Notes on the sheet:
  //   Register Mode (Types of OP = 00) = 2 bit (Type of OP) + 2 bit (Op) + 2 bit (Reg 1) + 2 bit (Reg 2) + 9 bit (Don't care)
  //   Immediate Mode (Types of OP = 01) = 2 bit (Type of OP) + 2 bit (Op) + 2 bit (Reg 1) + 6 bit (Imm value) + 5 bit (Don't care)
  //   Branching Mode (Types of OP = 10) = 2 bit (Type of OP) + 2 bit (Op) + 4 bit (Address) + 9 bit (Don't care)
  //   ADD (Op = 00) , AND (Op = 01), ROL (Op = 10)
  //   JMP (Op = 00), JZ (Op = 01)
  //                      JZ START :      -> 10010001000000000
  //   START :     AND R1,R1      -> 00010101000000000
  //   JMP_TO:   ADD R1,5         -> 01000100010100000
  //                      JMP JMP_TO  -> 10000001000000000
endmodule
